# Fritzing sketch pi-rain-sensor (saved by Fritzing 0.9.4)

parts:
  Raspberry_Pi_1 = Raspberry Pi 3 [part_number=RPI-3-V1.2]
  J1 = Piezo Speaker
  S1 = Toggle Switch [package=THT]
  YL-83_-_Detection_Board1 = YL-83 Rain Sensor - Detection Board
  YL-83_-_Control_Board1 = YL-83 Rain Sensor - Control Board

nets:
  3V3: Raspberry_Pi_1.3V3, YL-83_-_Control_Board1.VCC
  N1: Raspberry_Pi_1.GPIO13, J1.pin2
  GND: Raspberry_Pi_1.GND, S1.L1, YL-83_-_Control_Board1.GND
  N2: Raspberry_Pi_1.GPIO18, YL-83_-_Control_Board1.DO
  N3: J1.pin1, S1.COM
  N4: YL-83_-_Detection_Board1.POS, YL-83_-_Control_Board1.POS
  N5: YL-83_-_Detection_Board1.NEG, YL-83_-_Control_Board1.NEG

custom parts:
  YL-83 Rain Sensor - Detection Board: The YL-83 is a rain sensor that has more resistance when dry and less resistance when wet. The module runs at 5V.
  YL-83 Rain Sensor - Control Board: The YL-83 is a rain sensor that has more resistance when dry and less resistance when wet. The module runs at 5V.
